# Fritzing sketch Sketch (saved by Fritzing 0.9.10b)
breadboards: 1

parts:
  Mod1 = KY-016
  Mod2 = KY-024 Linear Hall Magnetic Sensor Module [package="Breakout board"]
  Componente1 = Arduino Uno (Rev3)
  Display1 = LCD screen 16x2 IIC [part_number=101290]

nets:
  N1: Mod1.connector2, Componente1.D5_PWM
  N2: Mod1.connector3, Componente1.D6_PWM
  GND: Mod1.connector4, Mod2.G, Componente1.GND, Display1.GND
  N3: Mod2.A0, Componente1.A0
  5V: Mod2.+, Componente1.5V, Display1.VCC
  N4: Componente1.A4/SDA, Display1.SDA
  N5: Componente1.A5/SCL, Display1.SCL

custom parts:
  KY-024 Linear Hall Magnetic Sensor Module: KY-024 Linear Hall Magnetic Sensor Module reacts iin the presence of a magnetic field.
  LCD screen 16x2 IIC: LCD screen with HD44780 controller enables showing text, symbols, value or anything else that comes from Croduino/Arduino. It is capable of showing 16 symbols in two lines and therefore can be used in many projects that need to send clearly visible and legible output information.. • Color of symbols: White • Backlight: Blue • Dimensions: 80 x 36 x 12 mm • Screen dimensions: 64.5 x 16 mm •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

// code stored in the sketch: teslaMeter.ino
#include <LiquidCrystal_I2C.h>    // Library LCD I2C


LiquidCrystal_I2C lcd(0x3f,16,2);   // Set screen LCD to use 16x2 resolution


// Set pins input
const int led2 = 6, led1 = 5;
// El iMax es hasta donde se acerca al voltaje medio (2.66v) y el iMin es desde donde empieza a medir por la cara sur, hacia arriba
int iMax = 539, iMin = 549;


void setup() {
  Serial.begin(9600);     // It initialize connection to serial monitor with 9600 baud
  pinMode(led1, OUTPUT);   // Set pin led as output
  pinMode(led2, OUTPUT);   // Set pin led as output
  digitalWrite(led1, LOW); // Led turn off
  digitalWrite(led2, LOW); // Led turn off
  Serial.println("Systems are ready!");
  lcd.init();             // Initialize the LCD
  lcd.backlight();        // Turn on background light of LCD
  lcd.setCursor(0,0);
  lcd.print("South -> Green");
  lcd.setCursor(0,1);
  lcd.print("North -> Blue");
  delay(1500);
  lcd.clear();            // Clean screen
}


void loop() {
  // Get voltage from sensor
  int sensorHall = analogRead(A0);
  Serial.print("Sensor Hall: ");
  Serial.println(sensorHall);


  voltage(sensorHall);
  teslaMeter(sensorHall);
  
  delay(500);    // Waiting 1/2 of second
}


void teslaMeter(int sHall){
  int shineLed = 0;
  int teslaMeter = 0;


  // Turn on led red dependenting of near magnet
  if (sHall >= 0 && sHall <= iMax){           // To turn on led if pole south is near (I think xd)
    shineLed = map(sHall, 0, iMax, 255, 0);  // Get value from sensor to escale values to led 255
    teslaMeter = map(sHall, 0, iMax, 7.6, 0);
    // Print values by serial
    ledShine(shineLed);
    Serial.print("South --> TeslaMeter [mT]: -");
    Serial.println(teslaMeter);
    //Set shine into led
    analogWrite(led1, shineLed);
    //Show the value in mT on lcd
    lcd.setCursor(0,1);
    lcd.print("TeslaMeter:");
    lcd.setCursor(11,1);
    lcd.print(teslaMeter);
    lcd.setCursor(13, 1);
    lcd.print("mT");
  } else {
    digitalWrite(led1, LOW);
  }


  if (sHall >= iMin && sHall <= 1023){          // The same that up but with pole north
    shineLed = map(sHall, iMin, 1023, 0, 255);
    teslaMeter = map(sHall, iMin, 1023, 0, 7.6);
    // Print values by serial
    ledShine(shineLed);
    Serial.print("North --> TeslaMeter [mT]: ");
    Serial.println(teslaMeter);
    //Set shine into led
    analogWrite(led2, shineLed);
    //Show the value in mT on lcd
    lcd.setCursor(0,1);
    lcd.print("TeslaMeter:");
    lcd.setCursor(11,1);
    lcd.print(teslaMeter);
    lcd.setCursor(13, 1);
    lcd.print("mT");
  } else {
    digitalWrite(led2, 0);
  }
}


void voltage (int sHall){
  // Convert the analog reading (which goes from 0 - 1023) to a voltage (0 - 5V):
  float volts = sHall * (5.0 / 1023);
  
  // Print out the value into lcd:
  lcd.clear();
  lcd.setCursor(0,0);
  lcd.print("Voltage:");
  lcd.setCursor(9,0);
  lcd.print(volts);
  lcd.setCursor(13, 0);
  lcd.print("[v]");
}


void ledShine (int shine){
  Serial.print("Shine Led: ");
  Serial.println(shine);
}
